// Digital circuit instruction_decoder.dig as structural Verilog
module instruction_decoder (
);

  wire I, I_t, R, R_t;

  not not_1 (I_t, I);
  not not_2 (R_t, R);

  // Notes on the sheet:
  //   I
  //   R
  //   T0
  //   T1
  //   T2
  //   T3
  //   T4
  //   D1
  //   D0
  //   D2
  //   D3
  //   D4
  //   D5
  //   D6
  //   D7
endmodule
